// Logisim project Processador Completo.circ as structural Verilog
module BR___Banco_de_Registradores (
  input  [4:0] RS,
  input  [4:0] RT,
  input  [4:0] RD,
  input  REG_WRTIE,
  input  [31:0] in_5,
  output [31:0] out_6,
  output [31:0] out_7
);

  wire regdxx;
  wire [31:0] reg1, reg2, reg3, reg4, reg5, reg6, reg7, reg8, reg9, reg10, reg11, reg12, reg13, reg14, reg15,
       reg16, reg17, reg18, reg19, reg20, reg21, reg22, reg23, reg24, reg25, reg26, reg27, reg28, reg29,
       reg30, reg31, reg32;

  Demultiplexer #(.select(5), .enable("false")) demultiplexer_1 (
    .out0(regdxx), .out1(regdxx), .out2(regdxx), .out3(regdxx), .out4(regdxx), .out5(regdxx), .out6(regdxx),
    .out7(regdxx), .out8(regdxx), .out9(regdxx), .out10(regdxx), .out11(regdxx), .out12(regdxx),
    .out13(regdxx), .out14(regdxx), .out15(regdxx), .out16(regdxx), .out17(regdxx), .out18(regdxx),
    .out19(regdxx), .out20(regdxx), .out21(regdxx), .out22(regdxx), .out23(regdxx), .out24(regdxx),
    .out25(regdxx), .out26(regdxx), .out27(regdxx), .out28(regdxx), .out29(regdxx), .out30(regdxx),
    .out31(regdxx), .in(REG_WRTIE), .sel(RD));
  Register #(.width(32), .Select("low")) register_1 (.D(in_5), .en(regdxx), .Q(reg1));  // open: clk, clr
  Register #(.width(32), .Select("low")) register_2 (.D(in_5), .en(regdxx), .Q(reg2));  // open: clk, clr
  Register #(.width(32), .Select("low")) register_3 (.en(regdxx), .Q(reg3));  // open: D, clk, clr
  Register #(.width(32), .Select("low")) register_4 (.D(in_5), .en(regdxx), .Q(reg4));  // open: clk, clr
  Register #(.width(32), .Select("low")) register_5 (.D(in_5), .en(regdxx), .Q(reg5));  // open: clk, clr
  Register #(.width(32), .Select("low")) register_6 (.D(in_5), .en(regdxx), .Q(reg6));  // open: clk, clr
  Register #(.width(32), .Select("low")) register_7 (.D(in_5), .en(regdxx), .Q(reg7));  // open: clk, clr
  Register #(.width(32), .Select("low")) register_8 (.D(in_5), .en(regdxx), .Q(reg8));  // open: clk, clr
  Register #(.width(32), .Select("low")) register_9 (.D(in_5), .en(regdxx), .Q(reg9));  // open: clk, clr
  Register #(.width(32), .Select("low")) register_10 (.D(in_5), .en(regdxx), .Q(reg10));  // open: clk, clr
  Register #(.width(32), .Select("low")) register_11 (.D(in_5), .en(regdxx), .Q(reg11));  // open: clk, clr
  Register #(.width(32), .Select("low")) register_12 (.D(in_5), .en(regdxx), .Q(reg12));  // open: clk, clr
  Register #(.width(32), .Select("low")) register_13 (.D(in_5), .en(regdxx), .Q(reg13));  // open: clk, clr
  Register #(.width(32), .Select("low")) register_14 (.D(in_5), .en(regdxx), .Q(reg14));  // open: clk, clr
  Register #(.width(32), .Select("low")) register_15 (.D(in_5), .en(regdxx), .Q(reg15));  // open: clk, clr
  Register #(.width(32), .Select("low")) register_16 (.D(in_5), .en(regdxx), .Q(reg16));  // open: clk, clr
  Register #(.width(32), .Select("low")) register_17 (.D(in_5), .en(regdxx), .Q(reg17));  // open: clk, clr
  Register #(.width(32), .Select("low")) register_18 (.D(in_5), .en(regdxx), .Q(reg18));  // open: clk, clr
  Register #(.width(32), .Select("low")) register_19 (.D(in_5), .en(regdxx), .Q(reg19));  // open: clk, clr
  Register #(.width(32), .Select("low")) register_20 (.D(in_5), .en(regdxx), .Q(reg20));  // open: clk, clr
  Register #(.width(32), .Select("low")) register_21 (.D(in_5), .en(regdxx), .Q(reg21));  // open: clk, clr
  Register #(.width(32), .Select("low")) register_22 (.D(in_5), .en(regdxx), .Q(reg22));  // open: clk, clr
  Register #(.width(32), .Select("low")) register_23 (.D(in_5), .en(regdxx), .Q(reg23));  // open: clk, clr
  Register #(.width(32), .Select("low")) register_24 (.D(in_5), .en(regdxx), .Q(reg24));  // open: clk, clr
  Register #(.width(32), .Select("low")) register_25 (.D(in_5), .en(regdxx), .Q(reg25));  // open: clk, clr
  Register #(.width(32), .Select("low")) register_26 (.D(in_5), .en(regdxx), .Q(reg26));  // open: clk, clr
  Register #(.width(32), .Select("low")) register_27 (.D(in_5), .en(regdxx), .Q(reg27));  // open: clk, clr
  Register #(.width(32), .Select("low")) register_28 (.D(in_5), .en(regdxx), .Q(reg28));  // open: clk, clr
  Register #(.width(32), .Select("low")) register_29 (.D(in_5), .en(regdxx), .Q(reg29));  // open: clk, clr
  Register #(.width(32), .Select("low")) register_30 (.D(in_5), .en(regdxx), .Q(reg30));  // open: clk, clr
  Register #(.width(32), .Select("low")) register_31 (.D(in_5), .en(regdxx), .Q(reg31));  // open: clk, clr
  Register #(.width(32), .Select("low")) register_32 (.D(in_5), .en(regdxx), .Q(reg32));  // open: clk, clr
  Multiplexer #(.select(5), .width(32), .enable("false")) multiplexer_1 (
    .in0(reg1), .in1(reg2), .in2(reg3), .in3(reg4), .in4(reg5), .in5(reg6), .in6(reg7), .in7(reg8),
    .in8(reg9), .in9(reg10), .in10(reg11), .in11(reg12), .in12(reg13), .in13(reg14), .in14(reg15),
    .in15(reg16), .in16(reg17), .in17(reg18), .in18(reg19), .in19(reg20), .in20(reg21), .in21(reg22),
    .in22(reg23), .in23(reg24), .in24(reg25), .in25(reg26), .in26(reg27), .in27(reg28), .in28(reg29),
    .in29(reg30), .in30(reg31), .in31(reg32), .out(out_6), .sel(RS));
  Multiplexer #(.select(5), .width(32), .enable("false")) multiplexer_2 (
    .in0(reg1), .in1(reg2), .in2(reg3), .in3(reg4), .in4(reg5), .in5(reg6), .in6(reg7), .in7(reg8),
    .in8(reg9), .in9(reg10), .in10(reg11), .in11(reg12), .in12(reg13), .in13(reg14), .in14(reg15),
    .in15(reg16), .in16(reg17), .in17(reg18), .in18(reg19), .in19(reg20), .in20(reg21), .in21(reg22),
    .in22(reg23), .in23(reg24), .in24(reg25), .in25(reg26), .in26(reg27), .in27(reg28), .in28(reg29),
    .in29(reg30), .in30(reg31), .in31(reg32), .out(out_7), .sel(RT));
endmodule

module \ULA___Unidade_Lógica_e_Aritmetica  (
  input  [31:0] in_1,
  input  [1:0] in_2,
  input  [31:0] in_3,
  output [31:0] out_4
);

  wire [31:0] adder_1_out, divider_1_out, multiplier_1_out, subtractor_1_out;

  Adder #(.width(32)) adder_1 (.a(in_1), .b(in_3), .out(adder_1_out));  // open: cin, cout
  Subtractor #(.width(32)) subtractor_1 (.a(in_1), .b(in_3), .out(subtractor_1_out));  // open: bin, bout
  Multiplier #(.width(32)) multiplier_1 (.a(in_1), .b(in_3), .out(multiplier_1_out));  // open: cin, cout
  Divider #(.width(32)) divider_1 (.a(in_1), .b(in_3), .out(divider_1_out));  // open: upper, rem
  Multiplexer #(.select(2), .width(32), .enable("false")) multiplexer_1 (
    .in0(adder_1_out), .in1(subtractor_1_out), .in2(multiplier_1_out), .in3(divider_1_out), .out(out_4),
    .sel(in_2));
endmodule
